# Fritzing sketch DMN_Version_1.5 (saved by Fritzing 0.9.3b)
breadboards: 1

parts:
  Raspberry_Pi_1 = Raspberry Pi 3 [part_number=RPI-3-V1.2]
  PIR1 = PIR sensor
  S2 = Momentary Switch [package=ksa_sealed_tac_switch]
  R15 = Resistor [tolerance=±5% resistance=1k package=THT]
  Raspberry_Pi_2 = Raspberry Pi 3 [part_number=RPI-3-V1.2]
  R17 = Resistor [tolerance=±5% resistance=220 package=THT]
  J2 = Piezo Speaker
  R18 = Resistor [tolerance=±5% resistance=220 package=THT]
  LED1 = LED - 3mm [color="Red (633nm)" package="3 mm [THT]"]
  VCC1 = Battery
  L1 = Solenoid
  M1 = 1 chan 5v relay module

nets:
  N1: Raspberry_Pi_1.GIPO27, PIR1.SIG
  GND: Raspberry_Pi_1.GND, PIR1.GND
  5V: Raspberry_Pi_1.5V, PIR1.VDD
  N2: S2.2, Raspberry_Pi_2.GIPO15
  N3: S2.4, R15.Pin_1
  3V3: R15.Pin_0, Raspberry_Pi_2.3v3, Raspberry_Pi_2.3V3, M1.pin_1
  N4: Raspberry_Pi_2.GIPO22, R18.Pin_0
  N5: Raspberry_Pi_2.GIPO6, M1.pin_3
  N6: Raspberry_Pi_2.GIPO21, R17.Pin_1
  N7: Raspberry_Pi_2.GND, Raspberry_Pi_2.GIPO23, J2.pin1, LED1.anode, M1.pin_2
  N8: R17.Pin_0, J2.pin2
  N9: R18.Pin_1, LED1.cathode
  N10: VCC1.+, M1.pin_4
  N11: L1.pin2, M1.pin_5

notes:
  Plug camera into camera port
  Plug official power supply
  Connect speaker via aux cable
  Connect finger scanner via uart USB attachment
  Piezo buzzer, 220 ohm resistor
  momentary switch, connected to 3.3v power, 1 Kilo ohm resistor, connected to gpio, Responsible for input from user inside the room
  PIR sensor
  door sensor (represented as wires, yellow is the door components itself)
  led to indicate door open or closed
  Raspberry Pi Inside the room
  Raspberry Pi Outside the room
  In the real version, a 12v dc power supply is used
  12v sub-600 mA electric strike lock
  5v relay single channel relay
  The exact LCD screen we will use is unavailable in Fritzing but we have pinouts available in our documentation

custom parts:
  1 chan 5v relay module: 1 Channel 5V Relay Module Board Shield with Optocoupler Support High and Low Level Trigger for Arduino.
